# Fritzing sketch soap_dispenser_timer (saved by Fritzing 0.8.7b)

parts:
  R2 = Resistor [tolerance=±5% resistance=220 package=THT]
  R3 = Resistor [tolerance=±5% resistance=220 package=THT]
  Vibration_Switch = Tilt Switch [package=THT]
  Metro_Mini = Adafruit Metro Mini [part_number="Adafruit #2590"]
  RGB_LED_(Common_Cathode) = RGB LED (com. cathode, rgb) [package="5 mm [THT]"]
  R4 = Resistor [tolerance=±5% resistance=220 package=THT]

nets:
  N1: R2.Pin_0, Metro_Mini.IO1
  N2: R2.Pin_1, RGB_LED_(Common_Cathode).green_anode
  N3: R3.Pin_0, Metro_Mini.IO0
  N4: R3.Pin_1, RGB_LED_(Common_Cathode).blue_anode
  N5: Vibration_Switch.Pin_1, Metro_Mini.AD0
  N6: Vibration_Switch.Pin_2, Metro_Mini.+5V
  N7: Metro_Mini.IO2, R4.Pin_0
  N8: Metro_Mini.GND, RGB_LED_(Common_Cathode).common_cathode
  N9: RGB_LED_(Common_Cathode).red_anode, R4.Pin_1

custom parts:
  Adafruit Metro Mini: We sure love the ATmega328 here at Adafruit, and we use them a lot for our own projects. The processor has plenty of GPIO, Analog inputs, hardware UART SPI and I2C, timers and PWM galore - just enough for most simple projects. When we need to go small, we use a Pro Trinket 3V or 5V, but if you want to have USB-to-Serial built in, we reach for an Adafruit METRO Mini. METRO Mini is the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
